// Logisim project simulacao_logim.circ as structural Verilog: 1 circuit, main circuit main
module main (
);

  wire a, A0, A1, A2, and_1_out, and_2_out, and_3_out, and_4_out, and_5_out, and_6_out, and_7_out, and_8_out,
       and_9_out, and_10_out, and_11_out, b, c, d, e, f, g, pt;

  Button button_1 (.out(A2));
  Button button_2 (.out(A1));
  Button button_3 (.out(A0));
  and and_1 (and_1_out, A2, A0);
  and and_2 (and_2_out, ~A2, ~A1);  // AND_Gate
  and and_3 (and_3_out, A2, A1);
  and and_4 (and_4_out, ~A1, A0);  // AND_Gate
  and and_5 (and_5_out, A1, ~A0);  // AND_Gate
  or or_1 (a, and_1_out, ~A1);  // OR_Gate
  or or_2 (b, and_2_out, and_3_out, A0);
  or or_3 (c, ~A2, A1);  // OR_Gate
  or or_4 (d, and_4_out, and_5_out, A2);
  and and_6 (and_6_out, ~A2, ~A1);  // AND_Gate
  and and_7 (and_7_out, ~A2, ~A0);  // AND_Gate
  and and_8 (and_8_out, ~A1, ~A0);  // AND_Gate
  and and_9 (and_9_out, ~A2, ~A0);  // AND_Gate
  and and_10 (and_10_out, A1, ~A0);  // AND_Gate
  and and_11 (and_11_out, A2, A0);
  or or_5 (e, ~A1, ~A0);  // OR_Gate
  or or_6 (f, and_6_out, and_7_out, and_8_out);
  or or_7 (g, and_9_out, and_10_out, and_11_out);
  _7_Segment_Display u_7_segment_display_1 (.g(g), .f(f), .a(a), .b(b), .e(e), .d(d), .c(c), .dp(pt));
endmodule
