// Logisim project somador_1_bit.circ as structural Verilog: 1 circuit, main circuit main
// Co
module main (
);

  wire A_out, B_out, Ci_out, nand_1_out, nand_2_out, nand_3_out, nand_4_out, nand_5_out, nand_6_out,
       nand_7_out, nand_8_out, nand_9_out;

  Button A (.out(A_out));
  Button B (.out(B_out));
  Button Ci (.out(Ci_out));
  nand nand_1 (nand_1_out, A_out, B_out);
  nand nand_2 (nand_2_out, A_out, nand_1_out);
  nand nand_3 (nand_3_out, nand_1_out, B_out);
  nand nand_4 (nand_4_out, nand_2_out, nand_3_out);
  nand nand_5 (nand_5_out, nand_4_out, Ci_out);
  nand nand_6 (nand_6_out, nand_4_out, nand_5_out);
  nand nand_7 (nand_7_out, nand_5_out, Ci_out);
  nand nand_8 (nand_8_out, nand_5_out, nand_1_out);
  LED S (.in(nand_9_out));
  nand nand_9 (nand_9_out, nand_6_out, nand_7_out);
  LED Co (.in(nand_8_out));
endmodule
